# Fritzing sketch Light-Box Sketch 2 (saved by Fritzing 0.9.1b)
breadboards: 1

parts:
  Part1 = Arduino Mega 2560 (Rev3)
  S1 = Pushbutton [package="[THT]"]
  S2 = Pushbutton [package="[THT]"]
  S3 = Pushbutton [package="[THT]"]
  S4 = Pushbutton [package="[THT]"]
  R1 = Resistor [tolerance=±5% resistance=10k package=THT]
  R2 = Resistor [tolerance=±5% resistance=10k package=THT]
  R3 = Resistor [tolerance=±5% resistance=10k package=THT]
  R4 = Resistor [tolerance=±5% resistance=10k package=THT]
  LCD1 = LCD screen  # not connected
  U1 = WS2801 [package=sop-14]
  LED1 = RGB LED (com. cathode, rgb) [package="5 mm [THT]"]

nets:
  GND: Part1.GND, R1.Pin_0, R2.Pin_0, R3.Pin_0, R4.Pin_0, U1.GND, LED1.common_cathode
  5V: Part1.5V, S1.Pin_3, S1.Pin_4, S2.Pin_3, S2.Pin_4, S3.Pin_3, S3.Pin_4, S4.Pin_3, S4.Pin_4, U1.VCC
  N1: Part1.D6_PWM, U1.SDI
  N2: Part1.D7_PWM, U1.CKI
  N3: Part1.D22, S4.Pin_1, S4.Pin_2, R4.Pin_1
  N4: Part1.D24, S3.Pin_1, S3.Pin_2, R3.Pin_1
  N5: Part1.D26, S2.Pin_1, S2.Pin_2, R2.Pin_1
  N6: Part1.D28, S1.Pin_1, S1.Pin_2, R1.Pin_1
  N7: U1.BOUT, LED1.green_anode
  N8: U1.GOUT, LED1.blue_anode
  N9: U1.ROUT, LED1.red_anode
